# Fritzing sketch CanSat (saved by Fritzing 1.0.1rc)
circuit board: 7.26596cm x 3.36989cm
breadboards: 1

parts:
  GPS = Adafruit Ultimate GPS v3 [part_number="Adafruit #746"]
  LoRa_RFM9x = Adafruit RFM9x LoRa Radio [part_number="Adafruit #3072 and #3073"]
  BNO08x_IMU = Adafruit BNO085 9-DOF Orientation IMU Fusion [part_number="Addfruit #4754"]
  CanSat_Fulford_Pico = Raspberry Pi Pico H
  BMP280 = BMP280 Breakout Board [part_number=BMP280]

nets:
  VIN: GPS.VIN, LoRa_RFM9x.VIN, BNO08x_IMU.VCC, CanSat_Fulford_Pico.3V3, BMP280.VCC
  GND: GPS.GND, LoRa_RFM9x.GND, BNO08x_IMU.GND, CanSat_Fulford_Pico.GND, BMP280.GND
  N1: GPS.RX, CanSat_Fulford_Pico.GP0
  N2: GPS.TX, CanSat_Fulford_Pico.GP1
  N3: LoRa_RFM9x.SCK, CanSat_Fulford_Pico.GP26_A0
  N4: LoRa_RFM9x.MISO, CanSat_Fulford_Pico.GP28_A2
  N5: LoRa_RFM9x.MOSI, CanSat_Fulford_Pico.GP27_A1
  N6: LoRa_RFM9x.CS, CanSat_Fulford_Pico.GP22
  N7: LoRa_RFM9x.RST, CanSat_Fulford_Pico.GP21
  N8: BNO08x_IMU.SDA/MISO/TX, CanSat_Fulford_Pico.GP18, BMP280.SDA
  N9: BNO08x_IMU.SCL/SCK/RX, CanSat_Fulford_Pico.GP19, BMP280.SCL

notes:
  CanSat

custom parts:
  Adafruit Ultimate GPS v3: We carry a few different GPS modules here in the Adafruit shop, but none that satisfied our every desire - that's why we designed this little GPS breakout board. We believe this is the Ultimate GPS module, so we named it that. It's got everything you want and more: -165 dBm sensitivity, 10 Hz updates, 66 channels 5V friendly design and only 20mA current draw Breadboard friendly + two mounting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
  Adafruit RFM9x LoRa Radio: Sending data over long distances is like magic, and now you can be a magician with this range of powerful and easy-to-use radio modules. Sure, sometimes you want to talk to a computer (a good time to use WiFi) or perhaps communicate with a Phone (choose Bluetooth Low Energy!) but what if you want to send data very far? Most WiFi, Bluetooth, Zigbee and other wireless chipsets use 2.4GHz, which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
  Raspberry Pi Pico H: Raspberry Pi Pico H. Based around the RP2040 microcontroller the Pico H is a low cost microcontroller device bringing Raspberry Pi quality, cost, and easy of use to the microcontroller space.
  BMP280 Breakout Board: A fast and precise environmental sensor that can measure temperature, pressure, and altitude. Our BMP280 breakout is Raspberry-Pi and Arduino-compatible.
