# Fritzing sketch GroundStation (saved by Fritzing 1.0.1rc)

parts:
  Part1 = Adafruit RFM9x LoRa Radio [part_number="Adafruit #3072 and #3073"]
  Pico_Display1 = Raspberry Pi Pico Display

nets:
  VIN: Part1.VIN, Pico_Display1.3V3
  GND: Part1.GND, Pico_Display1.GND
  N1: Part1.SCK, Pico_Display1.GP26_A0
  N2: Part1.MISO, Pico_Display1.GP28_A2
  N3: Part1.MOSI, Pico_Display1.GP27_A1
  N4: Part1.CS, Pico_Display1.GP22
  N5: Part1.RST, Pico_Display1.GP21

custom parts:
  Adafruit RFM9x LoRa Radio: Sending data over long distances is like magic, and now you can be a magician with this range of powerful and easy-to-use radio modules. Sure, sometimes you want to talk to a computer (a good time to use WiFi) or perhaps communicate with a Phone (choose Bluetooth Low Energy!) but what if you want to send data very far? Most WiFi, Bluetooth, Zigbee and other wireless chipsets use 2.4GHz, which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
  Raspberry Pi Pico Display: Raspberry Pi Pico H. Based around the RP2040 microcontroller the Pico H is a low cost microcontroller device bringing Raspberry Pi quality, cost, and easy of use to the microcontroller space.
